// Logisim project 8_bit_CPU.circ as structural Verilog: 9 circuits, main circuit main
module main (
);

  wire [7:0] pc_1_out_put;
  wire [15:0] rom_1_data;

  PC pc_1 (.OUT_PUT(pc_1_out_put));  // open: RESET, LOAD, UP_DOWN, Enable, IN_PUT
  ROM #(.dataWidth(16)) rom_1 (.addr(pc_1_out_put), .data(rom_1_data));
  RAM ram_1 ();  // open: addr, data, sel, clk, ld, clr
  New_ALU new_alu_1 ();  // open: INPUT_A, INPUT_B, OPCODE, OUT_PUT
endmodule

module MemoryCell (
  input  Clock,
  input  WriteEnablePin,
  input  D_in,
  input  OutputEnablePin,
  input  reset,
  output D_out,
  output Stored_Data
);

  wire and_1_out, and_2_out, not_1_out, or_1_out;

  not not_1 (not_1_out, WriteEnablePin);
  and and_1 (and_1_out, Stored_Data, not_1_out);
  and and_2 (and_2_out, WriteEnablePin, D_in);
  or or_1 (or_1_out, and_1_out, and_2_out);
  D_Flip_Flop d_ff_1 (.D(or_1_out), .clk(Clock), .Q(Stored_Data), .reset(reset));  // open: Qn, preset
  assign D_out = OutputEnablePin ? Stored_Data : 1'bz;  // Controlled_Buffer controlled_buffer_1

  // Notes on the sheet:
  //   Memory Cell
endmodule

module registerrr (
  input  M_Write_Enable,
  input  M_Output_Enable,
  input  [15:0] Memory_I,
  input  [7:0] Manual_M_Address,
  input  in_5,
  input  in_6,
  input  in_7,
  output [7:0] Lower_Bits,
  output [7:0] Higher_Bits
);

  wire Clk;
  wire [7:0] R0_In, R0_Out, R1_In, R1_Out, R2_In, R2_Out, R3_In, R3_Out, R4_In, R4_Out, R5_In, R5_Out, R6_In,
       R6_Out, R7_In, R7_Out;

  Clock clock_1 (.out(Clk));
  Register R0 (.D(R0_In), .clk(Clk), .Q(R0_Out));  // open: en, clr
  Register R4 (.D(R4_In), .clk(Clk), .Q(R4_Out));  // open: en, clr
  Register R1 (.D(R1_In), .clk(Clk), .Q(R1_Out));  // open: en, clr
  Register R5 (.D(R5_In), .clk(Clk), .Q(R5_Out));  // open: en, clr
  Register R2 (.D(R2_In), .clk(Clk), .Q(R2_Out));  // open: en, clr
  Register R6 (.D(R6_In), .clk(Clk), .Q(R6_Out));  // open: en, clr
  Register R3 (.D(R3_In), .clk(Clk), .Q(R3_Out));  // open: en, clr
  Register R7 (.D(R7_In), .clk(Clk), .Q(R7_Out));  // open: en, clr
  RAM #(.dataWidth(16)) ram_1 (
    .addr(Manual_M_Address), .we(M_Write_Enable), .oe(M_Output_Enable), .clk(Clk),
    .data({Higher_Bits, Lower_Bits}));
  Multiplexer #(.select(3), .width(8)) multiplexer_1 (
    .in0(R0_Out), .in1(R1_Out), .in2(R2_Out), .in3(R3_Out), .in4(R4_Out), .in5(R5_Out), .in6(R6_Out),
    .in7(R7_Out), .out(Manual_M_Address), .sel({in_5, in_6, in_7}));  // open: en

  // Other names for the same wires on the sheet: M_Address[7:0] = Manual_M_Address; M_Input[15:0] = Memory_I;
  //   M_Output[15:0] = {Higher_Bits, Lower_Bits}
endmodule

module PC (
  input  RESET,
  input  LOAD,
  input  UP_DOWN,
  input  Enable,
  input  [7:0] IN_PUT,
  output [7:0] OUT_PUT
);

  wire clock_1_out, counter_1_carry;

  Clock clock_1 (.out(clock_1_out));
  Counter counter_1 (
    .clr(RESET), .load(LOAD), .up(UP_DOWN), .count(Enable), .clk(clock_1_out), .D(IN_PUT),
    .carry(counter_1_carry), .Q(OUT_PUT));
endmodule

module Full_adder (
  input  A,
  input  B,
  input  Ci,
  output E,
  output Co
);

  wire and_1_out, and_2_out, xor_1_out;

  xor xor_1 (xor_1_out, A, B);
  xor xor_2 (E, xor_1_out, Ci);
  and and_1 (and_1_out, xor_1_out, Ci);
  or or_1 (Co, and_1_out, and_2_out);
  and and_2 (and_2_out, A, B);
endmodule

module ALU_8_bits (
  input  Su,
  input  A7,
  input  A6,
  input  A5,
  input  A4,
  input  A3,
  input  A2,
  input  A1,
  input  A0,
  input  En,
  input  B7,
  input  B6,
  input  B5,
  input  B4,
  input  B3,
  input  B2,
  input  B1,
  input  B0,
  output CF,
  output ZF,
  output S7,
  output S6,
  output S5,
  output S4,
  output S3,
  output S2,
  output S1,
  output S0,
  output E7,
  output E6,
  output E5,
  output E4,
  output E3,
  output E2,
  output E1,
  output E0
);

  wire full_adder_1_p2, full_adder_1_p3, full_adder_1_p5, full_adder_2_p2, full_adder_3_p2, full_adder_3_p5,
       full_adder_4_p2, full_adder_4_p5, full_adder_5_p5, full_adder_6_p5, full_adder_7_p5, xor_1_out,
       xor_2_out, xor_3_out, xor_4_out;

  // Full_adder full_adder_1: pin names not known; wires that end beside it: A1, full_adder_1_p2, full_adder_1_p3, S1, full_adder_1_p5
  // Full_adder full_adder_2: pin names not known; wires that end beside it: A0, full_adder_2_p2, Su, S0, full_adder_1_p3
  xor xor_1 (xor_1_out, Su, B7);
  // Full_adder full_adder_3: pin names not known; wires that end beside it: A2, full_adder_3_p2, full_adder_1_p5, S2, full_adder_3_p5
  xor xor_2 (xor_2_out, Su, B6);
  xor xor_3 (xor_3_out, Su, B5);
  // Full_adder full_adder_4: pin names not known; wires that end beside it: A3, full_adder_4_p2, full_adder_3_p5, S3, full_adder_4_p5
  xor xor_4 (xor_4_out, Su, B4);
  xor xor_5 (full_adder_4_p2, Su, B3);
  // Full_adder full_adder_5: pin names not known; wires that end beside it: A4, xor_4_out, full_adder_4_p5, S4, full_adder_5_p5
  // Full_adder full_adder_6: pin names not known; wires that end beside it: A5, xor_3_out, full_adder_5_p5, S5, full_adder_6_p5
  xor xor_6 (full_adder_1_p2, Su, B1);
  xor xor_7 (full_adder_3_p2, Su, B2);
  // Full_adder full_adder_7: pin names not known; wires that end beside it: A6, xor_2_out, full_adder_6_p5, S6, full_adder_7_p5
  xor xor_8 (full_adder_2_p2, Su, B0);
  // Full_adder full_adder_8: pin names not known; wires that end beside it: A7, xor_1_out, full_adder_7_p5, S7, CF
  nor nor_1 (ZF, S7, S6, S5, S4, S3, S2, S1, S0);
  assign E7 = En ? S7 : 1'bz;  // Controlled_Buffer controlled_buffer_1
  assign E6 = En ? S6 : 1'bz;  // Controlled_Buffer controlled_buffer_2
  assign E5 = En ? S5 : 1'bz;  // Controlled_Buffer controlled_buffer_3
  assign E4 = En ? S4 : 1'bz;  // Controlled_Buffer controlled_buffer_4
  assign E3 = En ? S3 : 1'bz;  // Controlled_Buffer controlled_buffer_5
  assign E2 = En ? S2 : 1'bz;  // Controlled_Buffer controlled_buffer_6
  assign E1 = En ? S1 : 1'bz;  // Controlled_Buffer controlled_buffer_7
  assign E0 = En ? S0 : 1'bz;  // Controlled_Buffer controlled_buffer_8
endmodule

module New_ALU (
  input  [7:0] INPUT_A,
  input  [7:0] INPUT_B,
  input  [2:0] OPCODE,
  output [7:0] OUT_PUT
);

  wire [7:0] adder_1_out, and_1_out, shifter_1_out, shifter_2_out, subtractor_1_out;

  Adder adder_1 (.a(INPUT_A), .b(INPUT_B), .out(adder_1_out));  // open: cin, cout
  Subtractor subtractor_1 (.a(INPUT_A), .b(INPUT_B), .out(subtractor_1_out));  // open: bin, bout
  Shifter shifter_1 (.in(INPUT_A), .\dist (3'b001), .out(shifter_1_out));
  Shifter #(.shift("lr")) shifter_2 (.in(INPUT_A), .\dist (3'b001), .out(shifter_2_out));
  assign and_1_out = INPUT_A & INPUT_B;  // AND_Gate and_1, 8 bits wide
  Multiplexer #(.select(3), .width(8)) multiplexer_1 (
    .in0(adder_1_out), .in1(subtractor_1_out), .in2(shifter_1_out), .in3(shifter_2_out), .in4(and_1_out),
    .out(OUT_PUT), .sel(OPCODE));  // open: in5, in6, in7, en

  // Notes on the sheet:
  //   000 - Adder 
  //   001 - Subtractor
  //   010 - Logical Left Shift
  //   011 - Logical Right Shift
  //   100 - AND operation
endmodule

module CU (
  input  [7:0] in_1
);
endmodule

module reg_8Bit (
  input  [2:0] read_reg01,
  input  [2:0] read_reg02,
  input  [2:0] write_reg,
  input  [7:0] write_data,
  input  regWrite,
  input  clock,
  output [7:0] read_data01,
  output [7:0] read_data02
);

  wire and_1_out, and_2_out, and_3_out, and_4_out, and_5_out, and_6_out, and_7_out, and_8_out,
       decoder_1_out0, decoder_1_out1, decoder_1_out2, decoder_1_out3, decoder_1_out4, decoder_1_out5,
       decoder_1_out6, decoder_1_out7, undriven;
  wire [7:0] register_1_q, register_2_q, register_3_q, register_4_q, register_5_q, register_6_q,
       register_7_q, register_8_q;

  Decoder #(.select(3)) decoder_1 (
    .out0(decoder_1_out0), .out1(decoder_1_out1), .out2(decoder_1_out2), .out3(decoder_1_out3),
    .out4(decoder_1_out4), .out5(decoder_1_out5), .out6(decoder_1_out6), .out7(decoder_1_out7),
    .sel(read_reg01));  // open: en
  and and_1 (and_1_out, decoder_1_out0, regWrite);
  and and_2 (and_2_out, decoder_1_out1, regWrite);
  and and_3 (and_3_out, decoder_1_out2, regWrite);
  and and_4 (and_4_out, decoder_1_out3, regWrite);
  and and_5 (and_5_out, decoder_1_out4, regWrite);
  and and_6 (and_6_out, decoder_1_out5, regWrite);
  and and_7 (and_7_out, decoder_1_out6, regWrite);
  and and_8 (and_8_out, decoder_1_out7, regWrite);
  Register register_1 (.D(write_data), .en(and_1_out), .clk(clock), .Q(register_1_q));  // open: clr
  Register register_2 (.D(write_data), .en(and_2_out), .clk(clock), .Q(register_2_q));  // open: clr
  Register register_3 (.D(write_data), .en(and_3_out), .clk(clock), .Q(register_3_q));  // open: clr
  Register register_4 (.D(write_data), .en(and_4_out), .clk(clock), .Q(register_4_q), .clr(undriven));
  Register register_5 (.D(write_data), .en(and_5_out), .clk(clock), .Q(register_5_q));  // open: clr
  Register register_6 (.D(write_data), .en(and_6_out), .clk(clock), .Q(register_6_q));  // open: clr
  Register register_7 (.D(write_data), .en(and_7_out), .clk(clock), .Q(register_7_q));  // open: clr
  Register register_8 (.D(write_data), .en(and_8_out), .clk(clock), .Q(register_8_q));  // open: clr
  Multiplexer #(.select(3), .width(8), .enable("false")) multiplexer_1 (
    .in0(register_1_q), .in1(register_2_q), .in2(register_3_q), .in3(register_4_q), .in4(register_5_q),
    .in5(register_6_q), .in6(register_7_q), .in7(register_8_q), .out(read_data01), .sel(read_reg01));
  Multiplexer #(.select(3), .width(8), .enable("false")) multiplexer_2 (
    .in0(register_1_q), .in1(register_2_q), .in2(register_3_q), .in3(register_4_q), .in4(register_5_q),
    .in5(register_6_q), .in6(register_7_q), .in7(register_8_q), .out(read_data02), .sel(read_reg02));

  assign write_reg = read_reg01;
endmodule
