// Logisim project computer_8bits.circ as structural Verilog: 4 circuits, main circuit ALU_8_bits
module ALU_8_bits (
  input  Su,
  input  A7,
  input  A6,
  input  A5,
  input  A4,
  input  A3,
  input  A2,
  input  A1,
  input  A0,
  input  En,
  input  B7,
  input  B6,
  input  B5,
  input  B4,
  input  B3,
  input  B2,
  input  B1,
  input  B0,
  output CF,
  output ZF,
  output S7,
  output S6,
  output S5,
  output S4,
  output S3,
  output S2,
  output S1,
  output S0,
  output E7,
  output E6,
  output E5,
  output E4,
  output E3,
  output E2,
  output E1,
  output E0
);

  wire full_adder_1_co, full_adder_2_co, full_adder_3_co, full_adder_4_co, full_adder_5_co, full_adder_6_co,
       full_adder_7_co, xor_1_out, xor_2_out, xor_3_out, xor_4_out, xor_5_out, xor_6_out, xor_7_out,
       xor_8_out;

  Full_adder full_adder_1 (.B(xor_8_out), .Ci(Su), .E(S0), .Co(full_adder_1_co), .A(A0));
  Full_adder full_adder_2 (.B(xor_6_out), .Ci(full_adder_1_co), .E(S1), .Co(full_adder_2_co), .A(A1));
  xor xor_1 (xor_1_out, Su, B7);
  Full_adder full_adder_3 (.B(xor_7_out), .Ci(full_adder_2_co), .E(S2), .Co(full_adder_3_co), .A(A2));
  xor xor_2 (xor_2_out, Su, B5);
  xor xor_3 (xor_3_out, Su, B6);
  Full_adder full_adder_4 (.B(xor_4_out), .Ci(full_adder_3_co), .E(S3), .Co(full_adder_4_co), .A(A3));
  xor xor_4 (xor_4_out, Su, B3);
  xor xor_5 (xor_5_out, Su, B4);
  Full_adder full_adder_5 (.B(xor_5_out), .Ci(full_adder_4_co), .E(S4), .Co(full_adder_5_co), .A(A4));
  Full_adder full_adder_6 (.B(xor_2_out), .Ci(full_adder_5_co), .E(S5), .Co(full_adder_6_co), .A(A5));
  xor xor_6 (xor_6_out, Su, B1);
  xor xor_7 (xor_7_out, Su, B2);
  Full_adder full_adder_7 (.B(xor_3_out), .Ci(full_adder_6_co), .E(S6), .Co(full_adder_7_co), .A(A6));
  xor xor_8 (xor_8_out, Su, B0);
  Full_adder full_adder_8 (.B(xor_1_out), .Ci(full_adder_7_co), .E(S7), .Co(CF), .A(A7));
  nor nor_1 (ZF, S7, S6, S5, S4, S3, S2, S1, S0);
  assign E7 = En ? S7 : 1'bz;  // Controlled_Buffer controlled_buffer_1
  assign E6 = En ? S6 : 1'bz;  // Controlled_Buffer controlled_buffer_2
  assign E5 = En ? S5 : 1'bz;  // Controlled_Buffer controlled_buffer_3
  assign E4 = En ? S4 : 1'bz;  // Controlled_Buffer controlled_buffer_4
  assign E3 = En ? S3 : 1'bz;  // Controlled_Buffer controlled_buffer_5
  assign E2 = En ? S2 : 1'bz;  // Controlled_Buffer controlled_buffer_6
  assign E1 = En ? S1 : 1'bz;  // Controlled_Buffer controlled_buffer_7
  assign E0 = En ? S0 : 1'bz;  // Controlled_Buffer controlled_buffer_8
endmodule

module Counter_8_bits (
  input  COut,
  input  CEnable,
  input  CWrite,
  input  CReset,
  input  Clock,
  input  I7,
  input  I6,
  input  I5,
  input  I4,
  input  I3,
  input  I2,
  input  I1,
  input  I0,
  output O7,
  output O6,
  output O5,
  output O4,
  output O3,
  output O2,
  output O1,
  output O0,
  output D7,
  output D6,
  output D5,
  output D4,
  output D3,
  output D2,
  output D1,
  output D0
);

  wire and_1_out, and_2_out, and_3_out, and_4_out, and_5_out, and_6_out, and_7_out, and_8_out, and_9_out,
       and_10_out, and_11_out, and_12_out, and_13_out, and_14_out, and_15_out, and_16_out, j_k_ff_2_qn,
       j_k_ff_3_qn, j_k_ff_4_qn, j_k_ff_5_qn, j_k_ff_6_qn, j_k_ff_7_qn, j_k_ff_8_qn, or_1_out, or_2_out,
       or_3_out, or_4_out, or_5_out, or_6_out, or_7_out, or_8_out;

  J_K_Flip_Flop j_k_ff_1 (
    .J(CEnable), .K(CEnable), .clk(j_k_ff_2_qn), .Q(D7), .preset(and_2_out), .reset(or_1_out));  // open: Qn
  or or_1 (or_1_out, CReset, and_1_out);
  and and_1 (and_1_out, CWrite, ~I7, Clock);  // AND_Gate
  and and_2 (and_2_out, CWrite, I7, Clock);
  J_K_Flip_Flop j_k_ff_2 (
    .J(CEnable), .K(CEnable), .clk(j_k_ff_3_qn), .Q(D6), .Qn(j_k_ff_2_qn), .preset(and_3_out),
    .reset(or_2_out));
  or or_2 (or_2_out, CReset, and_4_out);
  and and_3 (and_3_out, CWrite, I6, Clock);
  assign O7 = COut ? D7 : 1'bz;  // Controlled_Buffer controlled_buffer_1
  J_K_Flip_Flop j_k_ff_3 (
    .J(CEnable), .K(CEnable), .clk(j_k_ff_4_qn), .Q(D5), .Qn(j_k_ff_3_qn), .preset(and_5_out),
    .reset(or_3_out));
  and and_4 (and_4_out, CWrite, ~I6, Clock);  // AND_Gate
  and and_5 (and_5_out, CWrite, I5, Clock);
  assign O3 = COut ? D3 : 1'bz;  // Controlled_Buffer controlled_buffer_2
  assign O4 = COut ? D4 : 1'bz;  // Controlled_Buffer controlled_buffer_3
  assign O6 = COut ? D6 : 1'bz;  // Controlled_Buffer controlled_buffer_4
  assign O5 = COut ? D5 : 1'bz;  // Controlled_Buffer controlled_buffer_5
  J_K_Flip_Flop j_k_ff_4 (
    .J(CEnable), .K(CEnable), .clk(j_k_ff_5_qn), .Q(D4), .Qn(j_k_ff_4_qn), .preset(and_7_out),
    .reset(or_4_out));
  or or_3 (or_3_out, CReset, and_6_out);
  and and_6 (and_6_out, CWrite, ~I5, Clock);  // AND_Gate
  and and_7 (and_7_out, CWrite, I4, Clock);
  assign O1 = COut ? D1 : 1'bz;  // Controlled_Buffer controlled_buffer_6
  assign O0 = COut ? D0 : 1'bz;  // Controlled_Buffer controlled_buffer_7
  assign O2 = COut ? D2 : 1'bz;  // Controlled_Buffer controlled_buffer_8
  or or_4 (or_4_out, CReset, and_9_out);
  and and_8 (and_8_out, CWrite, I3, Clock);
  and and_9 (and_9_out, CWrite, ~I4, Clock);  // AND_Gate
  J_K_Flip_Flop j_k_ff_5 (
    .J(CEnable), .K(CEnable), .clk(j_k_ff_6_qn), .Q(D3), .Qn(j_k_ff_5_qn), .preset(and_8_out),
    .reset(or_5_out));
  or or_5 (or_5_out, CReset, and_10_out);
  and and_10 (and_10_out, CWrite, ~I3, Clock);  // AND_Gate
  J_K_Flip_Flop j_k_ff_6 (
    .J(CEnable), .K(CEnable), .clk(j_k_ff_7_qn), .Q(D2), .Qn(j_k_ff_6_qn), .preset(and_11_out),
    .reset(or_6_out));
  or or_6 (or_6_out, CReset, and_12_out);
  and and_11 (and_11_out, CWrite, I2, Clock);
  and and_12 (and_12_out, CWrite, ~I2, Clock);  // AND_Gate
  J_K_Flip_Flop j_k_ff_7 (
    .J(CEnable), .K(CEnable), .clk(j_k_ff_8_qn), .Q(D1), .Qn(j_k_ff_7_qn), .preset(and_13_out),
    .reset(or_7_out));
  or or_7 (or_7_out, CReset, and_14_out);
  and and_13 (and_13_out, CWrite, I1, Clock);
  and and_14 (and_14_out, CWrite, ~I1, Clock);  // AND_Gate
  J_K_Flip_Flop j_k_ff_8 (
    .J(CEnable), .K(CEnable), .clk(Clock), .Q(D0), .Qn(j_k_ff_8_qn), .preset(and_16_out), .reset(or_8_out));
  or or_8 (or_8_out, CReset, and_15_out);
  and and_15 (and_15_out, CWrite, ~I0, Clock);  // AND_Gate
  and and_16 (and_16_out, CWrite, I0, Clock);
endmodule

module Full_adder (
  input  A,
  input  B,
  input  Ci,
  output E,
  output Co
);

  wire and_1_out, and_2_out, xor_1_out;

  xor xor_1 (xor_1_out, A, B);
  xor xor_2 (E, xor_1_out, Ci);
  and and_1 (and_1_out, xor_1_out, Ci);
  or or_1 (Co, and_1_out, and_2_out);
  and and_2 (and_2_out, A, B);
endmodule

module Register_8_bits (
  input  Clock,
  input  Load,
  input  Reset,
  input  Enable,
  input  I7,
  input  I6,
  input  I5,
  input  I4,
  input  I3,
  input  I2,
  input  I1,
  input  I0,
  output B7,
  output B6,
  output B5,
  output B4,
  output B3,
  output B2,
  output B1,
  output B0,
  output O7,
  output O6,
  output O5,
  output O4,
  output O3,
  output O2,
  output O1,
  output O0
);

  Register #(.width(1)) register_1 (.D(I7), .en(Load), .clk(Clock), .Q(B7), .clr(Reset));
  Register #(.width(1)) register_2 (.D(I6), .en(Load), .clk(Clock), .Q(B6), .clr(Reset));
  Register #(.width(1)) register_3 (.D(I5), .en(Load), .clk(Clock), .Q(B5), .clr(Reset));
  Register #(.width(1)) register_4 (.D(I4), .en(Load), .clk(Clock), .Q(B4), .clr(Reset));
  Register #(.width(1)) register_5 (.D(I3), .en(Load), .clk(Clock), .Q(B3), .clr(Reset));
  Register #(.width(1)) register_6 (.D(I2), .en(Load), .clk(Clock), .Q(B2), .clr(Reset));
  Register #(.width(1)) register_7 (.D(I1), .en(Load), .clk(Clock), .Q(B1), .clr(Reset));
  Register #(.width(1)) register_8 (.D(I0), .en(Load), .clk(Clock), .Q(B0), .clr(Reset));
  assign O7 = Enable ? B7 : 1'bz;  // Controlled_Buffer controlled_buffer_1
  assign O6 = Enable ? B6 : 1'bz;  // Controlled_Buffer controlled_buffer_2
  assign O5 = Enable ? B5 : 1'bz;  // Controlled_Buffer controlled_buffer_3
  assign O4 = Enable ? B4 : 1'bz;  // Controlled_Buffer controlled_buffer_4
  assign O3 = Enable ? B3 : 1'bz;  // Controlled_Buffer controlled_buffer_5
  assign O2 = Enable ? B2 : 1'bz;  // Controlled_Buffer controlled_buffer_6
  assign O1 = Enable ? B1 : 1'bz;  // Controlled_Buffer controlled_buffer_7
  assign O0 = Enable ? B0 : 1'bz;  // Controlled_Buffer controlled_buffer_8
endmodule
